# Fritzing sketch Controller (saved by Fritzing 0.9.3b)
breadboards: 1

parts:
  Onderdeel1 = Arduino Uno (Rev3)
  S1 = Tilt Switch [package=THT]
  R1 = Resistor [tolerance=±5% resistance=220 package="2512 [SMD]"]
  R2 = Rotary Potentiometer (Small) [maximum_resistance=100kΩ package=THT]

nets:
  N1: Onderdeel1.A0, R2.wiper
  N2: Onderdeel1.D2, S1.Pin_2, R1.Pin_1
  N3: Onderdeel1.5V, R1.Pin_0
  N4: Onderdeel1.GND, S1.Pin_1, R2.leg1, R2.leg2
