# Fritzing sketch Displayer (saved by Fritzing 0.9.3b)
breadboards: 1

parts:
  Onderdeel1 = Arduino Uno (Rev3)
  Onderdeel2 = Bluetooth HC-05 Macho
  R1 = Resistor [tolerance=±5% resistance=220 package="0603 [SMD]"]
  R2 = Resistor [tolerance=±5% resistance=220 package="0603 [SMD]"]
  R3 = Resistor [tolerance=±5% resistance=220 package="0603 [SMD]"]

nets:
  N1: Onderdeel1.D2, Onderdeel2.TXD
  N2: Onderdeel1.D3_PWM, R1.Pin_0
  5V: Onderdeel1.5V, Onderdeel2.VCC
  GND: Onderdeel1.GND, Onderdeel2.GND, R3.Pin_1
  N3: Onderdeel2.RXD, R1.Pin_1, R2.Pin_1
  N4: R2.Pin_0, R3.Pin_0
